// Logisim project Project1.circ as structural Verilog
module FullAdder (
  input  A,
  input  B,
  input  Cin,
  output Sum,
  output Cout
);

  wire and_1_out, and_2_out, xor_1_out;

  xor xor_1 (xor_1_out, A, B);
  xor xor_2 (Sum, xor_1_out, Cin);
  and and_1 (and_1_out, xor_1_out, Cin);
  and and_2 (and_2_out, A, B);
  or or_1 (Cout, and_1_out, and_2_out);
endmodule

module RippleAdder8 (
  input  [7:0] A,
  input  Cin,
  input  [7:0] B,
  output [7:0] Y,
  output Cout
);

  wire fulladder_1_cout, fulladder_2_cout, fulladder_3_cout, fulladder_4_cout, fulladder_5_cout,
       fulladder_6_cout, fulladder_7_cout;

  FullAdder fulladder_1 (.A(A[0]), .B(B[0]), .Cin(Cin), .Sum(Y[0]), .Cout(fulladder_1_cout));
  FullAdder fulladder_2 (.A(A[1]), .B(B[1]), .Cin(fulladder_1_cout), .Sum(Y[1]), .Cout(fulladder_2_cout));
  FullAdder fulladder_3 (.A(A[2]), .B(B[2]), .Cin(fulladder_2_cout), .Sum(Y[2]), .Cout(fulladder_3_cout));
  FullAdder fulladder_4 (.A(A[3]), .B(B[3]), .Cin(fulladder_3_cout), .Sum(Y[3]), .Cout(fulladder_4_cout));
  FullAdder fulladder_5 (.A(A[4]), .B(B[4]), .Cin(fulladder_4_cout), .Sum(Y[4]), .Cout(fulladder_5_cout));
  FullAdder fulladder_6 (.A(A[5]), .B(B[5]), .Cin(fulladder_5_cout), .Sum(Y[5]), .Cout(fulladder_6_cout));
  FullAdder fulladder_7 (.A(A[6]), .B(B[6]), .Cin(fulladder_6_cout), .Sum(Y[6]), .Cout(fulladder_7_cout));
  FullAdder fulladder_8 (.A(A[7]), .B(B[7]), .Cin(fulladder_7_cout), .Sum(Y[7]), .Cout(Cout));
endmodule

module ArithmeticUnit (
  input  [7:0] B,
  input  S1,
  input  S0,
  input  [7:0] A,
  output [7:0] Y,
  output Cout
);

  wire and_1_out, not_2_out;
  wire [7:0] mux4to1_8_1_out_7, not_1_out;

  assign not_1_out = ~B;  // NOT_Gate not_1, 8 bits wide
  not not_2 (not_2_out, S1);
  and and_1 (and_1_out, not_2_out, S0);
  MUX4to1_8 mux4to1_8_1 (
    .S1(S1), .S0(S0), .I0(B), .I1(not_1_out), .I2(8'h1), .I3({8{1'b1}}), .out_7(mux4to1_8_1_out_7));
  RippleAdder8 rippleadder8_1 (.A(A), .Cin(and_1_out), .B(mux4to1_8_1_out_7), .Y(Y), .Cout(Cout));
endmodule

module MUX2to1 (
  input  S,
  input  A,
  input  B,
  output Y
);

  wire and_1_out, and_2_out, not_1_out;

  not not_1 (not_1_out, S);
  and and_1 (and_1_out, not_1_out, A);
  and and_2 (and_2_out, S, B);
  or or_1 (Y, and_1_out, and_2_out);
endmodule

module MUX2to1_8 (
  input  S,
  input  [7:0] A,
  input  [7:0] B,
  output [7:0] Y
);

  MUX2to1 mux2to1_1 (.S(S), .A(A[0]), .B(B[0]), .Y(Y[0]));
  MUX2to1 mux2to1_2 (.S(S), .A(A[1]), .B(B[1]), .Y(Y[1]));
  MUX2to1 mux2to1_3 (.S(S), .A(A[2]), .B(B[2]), .Y(Y[2]));
  MUX2to1 mux2to1_4 (.S(S), .A(A[3]), .B(B[3]), .Y(Y[3]));
  MUX2to1 mux2to1_5 (.S(S), .A(A[4]), .B(B[4]), .Y(Y[4]));
  MUX2to1 mux2to1_6 (.S(S), .A(A[5]), .B(B[5]), .Y(Y[5]));
  MUX2to1 mux2to1_7 (.S(S), .A(A[6]), .B(B[6]), .Y(Y[6]));
  MUX2to1 mux2to1_8 (.S(S), .A(A[7]), .B(B[7]), .Y(Y[7]));
endmodule

module MUX4to1_8 (
  input  S1,
  input  S0,
  input  [7:0] I0,
  input  [7:0] I1,
  input  [7:0] I2,
  input  [7:0] I3,
  output [7:0] out_7
);

  wire [7:0] mux2to1_8_1_y, mux2to1_8_2_y;

  MUX2to1_8 mux2to1_8_1 (.S(S0), .A(I0), .B(I1), .Y(mux2to1_8_1_y));
  MUX2to1_8 mux2to1_8_2 (.S(S0), .A(I2), .B(I3), .Y(mux2to1_8_2_y));
  MUX2to1_8 mux2to1_8_3 (.S(S1), .A(mux2to1_8_1_y), .B(mux2to1_8_2_y), .Y(out_7));
endmodule
